// Digital circuit 4RandomNumberGenerator.dig as structural Verilog
module _4RandomNumberGenerator (
  input  R0,
  input  R1,
  input  R2,
  output O4,
  output O3,
  output O2,
  output O1
);

  wire lelel_1_p3, lelel_1_p4, lelel_2_p3, lelel_3_p3, lelel_3_p4, lelel_4_p2, lelel_4_p4, lelel_5_p2,
       lelel_5_p4, lelel_6_p2, or_1_out;

  // lelel lelel_1: pin names not known; wires that end beside it: R2, O4, lelel_1_p3, lelel_1_p4
  // lelel lelel_2: pin names not known; wires that end beside it: R0, 1'b1, lelel_2_p3
  // lelel lelel_3: pin names not known; wires that end beside it: R1, lelel_1_p3, lelel_3_p3, lelel_3_p4, lelel_3_p3
  or or_1 (or_1_out, lelel_5_p2, lelel_3_p4);
  // lelel lelel_4: pin names not known; wires that end beside it: R2, lelel_4_p2, or_1_out, lelel_4_p4
  or or_2 (O3, lelel_4_p2, lelel_1_p4);
  // lelel lelel_5: pin names not known; wires that end beside it: R1, lelel_5_p2, lelel_2_p3, lelel_5_p4
  // lelel lelel_6: pin names not known; wires that end beside it: R2, lelel_6_p2, lelel_5_p4, O1
  or or_3 (O2, lelel_6_p2, lelel_4_p4);
endmodule
