// Digital circuit comparetoX.dig as structural Verilog
module comparetoX (
  input  [31:0] A,
  output Y
);

  wire comparator_1_gt, comparator_1_lt;

  Comparator #(.Bits(32)) comparator_1 (.a(A), .b(32'h5), .gt(comparator_1_gt), .eq(Y), .lt(comparator_1_lt));
endmodule

/* Code that sets the parameters or builds the circuit:
value:=3;
*/
