// Digital circuit decreasing_mem.dig as structural Verilog
module decreasing_mem (
  input  clock,
  input  [31:0] A,
  input  set,
  input  clr,
  output [31:0] \output 
);

  wire comp_eq, comp_gt, comp_lt;
  wire [31:0] d_ff_as_1_nq, d_ff_as_1_q, multiplexer_1_out;

  Comparator #(.Bits(32)) comp (.a(A), .b(d_ff_as_1_q), .gt(comp_gt), .eq(comp_eq), .lt(comp_lt));
  Multiplexer #(.Bits(32)) multiplexer_1 (.sel(comp_lt), .in_0(d_ff_as_1_q), .in_1(A), .out(multiplexer_1_out));
  D_FF_AS #(.Bits(32), .Default(2000000)) d_ff_as_1 (
    .Set(set), .D(multiplexer_1_out), .C(clock), .Clr(clr), .Q(d_ff_as_1_q), .nQ(d_ff_as_1_nq));
  Multiplexer #(.Bits(32)) multiplexer_2 (
    .sel(d_ff_as_1_q[31]), .in_0({1'b0, d_ff_as_1_q[30:0]}), .in_1(32'h7fffffff), .out(\output ));

  // Notes on the sheet:
  //   clock: Hz: 80000
  //   A: default 2147483647
endmodule
