// Digital circuit extract_path.dig as structural Verilog
module extract_path (
  input  [31:0] sel,
  input  clk,
  input  clr,
  output [31:0] out
);

  wire final_countup_1_out;
  wire [31:0] d_ff_as_1_nq;

  D_FF_AS #(.Bits(32)) d_ff_as_1 (
    .Set(1'b0), .C(final_countup_1_out), .Clr(clr), .Q(out), .nQ(d_ff_as_1_nq));  // open: D
  final_countup #(.generic("maxValue := args.number_of_inputs;")) final_countup_1 (
    .C(clk), .clr(clr), .out(final_countup_1_out));

  // Notes on the sheet:
  //   sel: default 1
endmodule

/* Test case:
clk clr sel i0 i1 i2 i3 i4 out

############################ Vertex 0 to every other Vertex 
loop(t,9)
  C 1 3 0 0 0 (t) 0 0 # reset line

  loop(a,4)
    C 0 3 0 0 0 (t) 0 0
  end loop

  C 0 3 0 0 0 (t) 0 (t)
end loop

############################ Vertex 0 to every other Vertex 
loop(t,9)
  C 1 1 (t) (t*2) 0 0 0 0 # reset line

  loop(a,4)
    C 0 1 (t) (t*2) 0 0 0 0
  end loop

  C 0 1 (t) (t*2) 0 0 0 (2*t)
end loop
*/

/* Test case:
clk clr sel i0 i1 out

############################ Vertex 0 to every other Vertex 
loop(t,9)
  C 1 0 (t) 0 0 # reset line

  loop(a,1)
    C 0 0 (t) 0 0
  end loop

  C 0 0 (t) 0 (t)
end loop

############################ Vertex 0 to every other Vertex 
loop(t,9)
  C 1 1 (t) (t*2) 0 # reset line

  loop(a,1)
    C 0 1 (t) (t*2) 0
  end loop

  C 0 1 (t) (t*2) (2*t)
end loop
*/

/* Code that sets the parameters or builds the circuit:
num_comp := args.number_of_inputs;

x_inp_start := 3;
y_inp_start := 3;
y_inp_add := 1;

x_mpout_start := 5;
y_mpout_start := 4;
y_mpout_add := 1;

x_wire_start:=5;
y_wire_start:=3;

select_bits:=1;
possible_inputs:=2;
while (possible_inputs<args.number_of_inputs){
    select_bits = select_bits + 1;
    possible_inputs = possible_inputs * 2;
}

splitter:=addComponent("Splitter", 1,0);
splitter.Bits = 32;
splitter.'Input Splitting' = ""+32;
splitter.'Output Splitting' = ""+select_bits+","+(32-select_bits);

multiplexer:=addComponent("Multiplexer", 3,3);
multiplexer.Bits = 32;
multiplexer.'Selector Bits' = select_bits;
multiplexer.flipSelPos = 1;

addWire(x_wire_start, y_wire_start + possible_inputs/2, 7, 2);

for (i:=0;i<args.number_of_inputs;i++){
    unary_buffer := 0;
    if (select_bits = 1){
        if (i=1){
            unary_buffer = 1;
        }
    }
    input:=addComponent("In", x_inp_start,y_inp_start+i*y_inp_add+unary_buffer);
    input.Bits=32;
    input.small=1;
    input.Label="i"+i;
}

for (i:=args.number_of_inputs;i<possible_inputs;i++){
    unary_buffer := 0;
    if (select_bits = 1){
        if (i=1){
            unary_buffer = 1;
        }
    }
    nonce:=addComponent("Const",x_inp_start,y_inp_start+i*y_inp_add+ unary_buffer);
    nonce.Bits=32;
    nonce.Value=0;
}
*/

/* Code that sets the parameters or builds the circuit:
number_of_inputs := 1;
*/
