// Digital circuit final_countup.dig as structural Verilog
module final_countup (
  input  clk,
  input  clr,
  output out
);

  wire and_1_out, comparator_1_eq, comparator_1_gt, comparator_1_lt, counter_1_ovf;
  wire [31:0] counter_1_out;

  and and_1 (and_1_out, comparator_1_gt, 1'b1);
  Counter #(.Bits(32)) counter_1 (.en(and_1_out), .C(clk), .clr(clr), .out(counter_1_out), .ovf(counter_1_ovf));
  Comparator #(.Bits(32)) comparator_1 (
    .a(32'h8), .b(counter_1_out), .gt(comparator_1_gt), .eq(comparator_1_eq), .lt(comparator_1_lt));
  or or_1 (out, comparator_1_eq, comparator_1_lt);
endmodule

/* Test case:
clk clr out

############################ Vertex 0 to every other Vertex 
C 1 0 # reset line

loop(a,3)
  C 0 0
end loop

C 0 1

C 1 0 # reset line

loop(a,3)
  C 0 0
end loop

C 0 1
*/

/* Code that sets the parameters or builds the circuit:
maxValue:=8;
*/

/* Test case:
clk clr out

############################ Vertex 0 to every other Vertex 
C 1 0 # reset line

loop(a,9)
  C 0 0
end loop

C 0 1

C 1 0 # reset line

loop(a,9)
  C 0 0
end loop

C 0 1
*/
