// Digital circuit final_finder.dig as structural Verilog
module final_finder (
  input  [31:0] \end ,
  output [31:0] out
);

  start_finder #(.generic("nodes := args.in_nodes;")) start_finder_1 (.in(\end ));
  wires_in #(.generic("in_nodes := args.in_nodes;")) wires_in_1 ();
endmodule

/* Code that sets the parameters or builds the circuit:
in_nodes:=3;
*/

/* Code that sets the parameters or builds the circuit:
inp_x:=20;

addWire(21,23+args.in_nodes/2,23,25);

for(i:=0;i<args.in_nodes; i++)
{
    addYwire := i;
    if(args.in_nodes%2=0)
    {
	if(i+1>args.in_nodes/2){
	   addYwire = addYwire+1;
	}
    }
    inp:=addComponent("In", inp_x+i*5,0);
    inp.Bits=32;
    inp.Label="in_"+i;

    mult:=addComponent("Multiplexer", inp_x+i*5+2,4);
    mult.Bits=32;

    addWire(inp_x+i*5,0,inp_x+i*5+2,6);
    addWire(19,8,inp_x+i*5+2,4);
    addWire(21,13+i,inp_x+i*5+3,6);
    addWire(inp_x+i*5+4,5,18,23+addYwire);
}
*/
