// Digital circuit node_module.dig as structural Verilog
module node_module (
  input  init,
  input  clk,
  input  clr,
  output [31:0] own
);

  wires_in #(.generic("in_nodes := args.neighbourhood_size;")) wires_in_1 ();
  decreasing_mem decreasing_mem_1 (.clock(clk), .set(clr), .clr(init), .\output (own));  // open: A
  wires_out #(.generic("out_nodes := args.neighbourhood_size; weights := args.edge_weights;")) wires_out_1 (.in(own));

  // Notes on the sheet:
  //   clk: Hz: 50000
endmodule

/* Code that sets the parameters or builds the circuit:
neighbourhood_size:=5;
edge_weights:=[4,8,1,1,1,1];
*/

/* Code that sets the parameters or builds the circuit:
x_output_start := 31;
y_output_start := 8;
y_output_add:= 1;

x_input_start := 16;
y_input_start := 6;
y_input_add:= 1;

y_input_offset:=0;

for (i:=0;i<args.neighbourhood_size;i++){
    output:=addComponent("Out",x_output_start,y_output_start+i*y_output_add);
    output.Bits=32;
    output.Label="o"+i;
    output.small=1;
}

for (i:=0;i<args.neighbourhood_size;i++){
    if(args.neighbourhood_size%2=0)
    {
	if(i>=args.neighbourhood_size/2){
	   y_input_offset = 1;
	}
    }
    output:=addComponent("In",x_input_start,y_input_start+i*y_input_add + y_input_offset);
    output.Bits=32;
    output.Label="i"+i;
    output.small=1;
}

addWire(x_input_start+3,y_input_start + args.neighbourhood_size/2,23,8);
*/

/* Test case:
clk clr init i0 i1 i2 i3 own o0 o1 o2 o3

############################ Vertex 0 to every other Vertex 

0 1 0 10 10 10 10 4294967295 4294967295 4294967295 4294967295 4294967295 # reset line

C 0 0 10 10 10 10 10 11 12 14 18

C 0 0 10 5 10 10 5 6 7 9 13

C 1 0 10 5 10 10 4294967295 4294967295 4294967295 4294967295 4294967295

C 0 0 50 50 50 50 50 51 52 54 58

C 0 0 50 3 50 50 3 4 5 7 11

C 0 1 50 3 50 50 0 1 2 4 8

C 1 0 50 3 50 50 4294967295 4294967295 4294967295 4294967295 4294967295

C 0 0 50 3 50 50 3 4 5 7 11
*/
