// Digital circuit node_module8.dig as structural Verilog
module node_module8 (
  input  [31:0] i1,
  input  [31:0] i2,
  input  [31:0] i3,
  input  [31:0] i4,
  input  [31:0] i5,
  input  [31:0] i6,
  input  [31:0] i7,
  input  [31:0] i8,
  input  start,
  input  clock,
  output [31:0] o1,
  output [31:0] o2,
  output [31:0] o3,
  output [31:0] o4,
  output [31:0] o5,
  output [31:0] o6,
  output [31:0] o7,
  output [31:0] o8,
  output [31:0] own
);

  wire [31:0] cheapselector_1_out, lookuptable_1_out, undriven;

  wires_in #(.generic("in_nodes := 8;")) wires_in_1 ();
  LookUpTable #(.Bits(32)) lookuptable_1 (.in0(start), .in1(start), .out(lookuptable_1_out));
  cheapSelector cheapselector_1 (.a(lookuptable_1_out), .b(undriven), .out(cheapselector_1_out));
  decreasing_mem decreasing_mem_1 (.clock(clock), .A(cheapselector_1_out), .\output (own));
  wires_out8 wires_out8_1 (.A(own), .Y(o1), .X(o2), .Z(o3), .U(o4), .V(o5), .Y2(o6), .X2(o7), .Z2(o8));

  // Notes on the sheet:
  //   i1: default 16
  //   i2: default 16
  //   i3: default 16
  //   i4: default 16
  //   i5: default 16
  //   i6: default 16
  //   i7: default 16
  //   i8: default 16
  //   clock: Hz: 50000
  //   contents of lookuptable_1 (hex, n*v repeats v):
  //   7fffffff
endmodule
