// Digital circuit wires_in8.dig as structural Verilog
module wires_in8 (
  input  [31:0] A,
  input  [31:0] B,
  input  [31:0] C,
  input  [31:0] D,
  input  [31:0] E,
  input  [31:0] F,
  input  [31:0] G,
  input  [31:0] H,
  output [31:0] out
);

  wire [31:0] cheapselector_1_out, cheapselector_2_out, cheapselector_3_out, cheapselector_4_out,
       cheapselector_5_out, cheapselector_6_out;

  cheapSelector cheapselector_1 (.a(A), .b(B), .out(cheapselector_1_out));
  cheapSelector cheapselector_2 (.a(C), .b(D), .out(cheapselector_2_out));
  cheapSelector cheapselector_3 (.a(E), .b(F), .out(cheapselector_3_out));
  cheapSelector cheapselector_4 (.a(G), .b(H), .out(cheapselector_4_out));
  cheapSelector cheapselector_5 (.a(cheapselector_1_out), .b(cheapselector_2_out), .out(cheapselector_5_out));
  cheapSelector cheapselector_6 (.a(cheapselector_3_out), .b(cheapselector_4_out), .out(cheapselector_6_out));
  cheapSelector cheapselector_7 (.a(cheapselector_5_out), .b(cheapselector_6_out), .out(out));

  // Notes on the sheet:
  //   A: default 2147483647
  //   B: default 2147483647
  //   C: default 2147483647
  //   D: default 2147483647
  //   E: default 2147483647
  //   F: default 2147483647
  //   G: default 2147483647
  //   H: default 2147483647
endmodule
