// Digital circuit wires_out8.dig as structural Verilog
module wires_out8 (
  input  [31:0] A,
  output [31:0] Y,
  output [31:0] X,
  output [31:0] Z,
  output [31:0] U,
  output [31:0] V,
  output [31:0] Y2,
  output [31:0] X2,
  output [31:0] Z2
);

  wire add_1_c_o;

  Add #(.Bits(32)) add_1 (.a(A), .b(32'h1), .c_i(1'b0), .s(U), .c_o(add_1_c_o));

  assign V = U;
  assign X = U;
  assign X2 = U;
  assign Y = U;
  assign Y2 = U;
  assign Z = U;
  assign Z2 = U;

  // Notes on the sheet:
  //   A: default 2147483647
endmodule
