// Digital circuit cheap_min.dig as structural Verilog
module cheap_min (
  input  [31:0] a,
  input  [31:0] b,
  input  [31:0] da,
  input  [31:0] db,
  output [31:0] min,
  output [31:0] dmin
);

  wire comparator_1_eq, comparator_1_gt, comparator_1_lt, or_1_out;

  Comparator #(.Bits(32)) comparator_1 (.a(a), .b(b), .gt(comparator_1_gt), .eq(comparator_1_eq), .lt(comparator_1_lt));
  Multiplexer #(.Bits(32)) multiplexer_1 (.sel(or_1_out), .in_0(a), .in_1(b), .out(min));
  Multiplexer #(.Bits(32)) multiplexer_2 (.sel(or_1_out), .in_0(da), .in_1(db), .out(dmin));
  or or_1 (or_1_out, comparator_1_gt, comparator_1_eq);

  // Notes on the sheet:
  //   a: default 2147483647
  //   b: default 2147483647
endmodule

/* Test case:
a b da db min dmin
0 0 0 0 0 0
0 2 0 0 0 0
2 0 0 0 0 0
2 2 5 7 2 7
*/
