// Digital circuit decode_path_string.dig as structural Verilog
module decode_path_string (
);
endmodule

/* Code that sets the parameters or builds the circuit:
substring_length := 3;
Bits := 32;
*/

/* Code that sets the parameters or builds the circuit:
input:=addComponent("In",0,0);
input.Bits=32;
input.Label="in";
input.small=1;
*/
