// Digital circuit example2.dig as structural Verilog
module example2 (
  input  clock,
  input  [31:0] VT,
  input  clr,
  input  [31:0] VS,
  output [31:0] SPW,
  output [31:0] SP
);

  wire _0_p4, _0_p5, _0_p6, _0_p7, _0_p8, _1_p6, demultiplexer_1_out_0, demultiplexer_1_out_1;

  Demultiplexer demultiplexer_1 (.sel(VS[0]), .in(1'b1), .out_0(demultiplexer_1_out_0), .out_1(demultiplexer_1_out_1));
  // node_module #(.generic("edge_weights := [4]; neighbourhood_size := 1; idx := 0;")) _0: pin names not known; wires that end beside it: demultiplexer_1_out_0, clock, clr, _0_p4, _0_p5, _0_p6, _0_p7, _0_p8
  // node_module #(.generic("edge_weights := [4]; neighbourhood_size := 1; idx := 1;")) _1: pin names not known; wires that end beside it: demultiplexer_1_out_1, clock, clr, _0_p7, _0_p8, _1_p6, _0_p5, _0_p4
  // extract_path #(.generic("number_of_inputs := 2;")) extract_path_1: pin names not known; wires that end beside it: VT, clock, clr, _0_p6, _1_p6, SPW
  // extract_path #(.generic("number_of_inputs := 2;")) extract_path_2: pin names not known; wires that end beside it: VT, clock, clr, _0_p7, _0_p5, SP
endmodule
