// Digital circuit node_module.dig as structural Verilog
module node_module (
  input  init,
  input  clk,
  input  clr,
  output [31:0] own,
  output [31:0] dout
);

  wire [31:0] decreasing_mem_1_p5;

  wires_in #(.generic("in_nodes := args.neighbourhood_size;")) wires_in_1 ();
  // decreasing_mem decreasing_mem_1: pin names not known; wires that end beside it: clk, clr, init, own, decreasing_mem_1_p5
  wires_out #(.generic("out_nodes := args.neighbourhood_size; weights := args.edge_weights; idx := args.idx;")) wires_out_1 (
    .in(own), .din(decreasing_mem_1_p5), .dout(dout));

  // Notes on the sheet:
  //   clk: Hz: 50000
endmodule

/* Code that sets the parameters or builds the circuit:
neighbourhood_size:=4;
edge_weights:=[4,8,1,1,1,1,1,1,1,1];
idx := 3;
*/

/* Code that sets the parameters or builds the circuit:
x_output_start := 31;
y_output_start := 8;
y_output_add:= 1;

x_input_start := 16;
y_input_start := 8;
y_input_add:= 2;

y_input_offset:=0;

for (i:=0;i<args.neighbourhood_size;i++){
    input:=addComponent("In",x_input_start,y_input_start+i*y_input_add + y_input_offset);
    input.Bits=32;
    input.Label="i"+i;
    input.small=1;
    dinput:=addComponent("In",x_input_start,y_input_start+i*y_input_add + y_input_offset+1);
    dinput.Bits=32;
    dinput.Label="di"+i;
    dinput.small=1;
}

addWire(x_input_start+3,y_input_start,23,8);
addWire(x_input_start+3,y_input_start+1,23,11);

for (i:=0;i<args.neighbourhood_size;i++){
    output:=addComponent("Out",x_output_start,y_output_start+i*y_output_add);
    output.Bits=32;
    output.Label="o"+i;
    output.small=1;
}
*/

/* Test case:
clk clr init i0 i1 i2 i3 own o0 o1 o2 o3

############################ Vertex 0 to every other Vertex 

0 1 0 10 10 10 10 4294967295 4294967295 4294967295 4294967295 4294967295 # reset line

C 0 0 10 10 10 10 10 11 12 14 18

C 0 0 10 5 10 10 5 6 7 9 13

C 1 0 10 5 10 10 4294967295 4294967295 4294967295 4294967295 4294967295

C 0 0 50 50 50 50 50 51 52 54 58

C 0 0 50 3 50 50 3 4 5 7 11

C 0 1 50 3 50 50 0 1 2 4 8

C 1 0 50 3 50 50 4294967295 4294967295 4294967295 4294967295 4294967295

C 0 0 50 3 50 50 3 4 5 7 11
*/
